# Fritzing sketch MidiHero (saved by Fritzing 0.9.10b)
circuit board: 4.12481cm x 5.34666cm
breadboards: 1

parts:
  Part1 = Arduino Nano (Rev3.0)
  ANT1 = Antenna
  ANT2 = Antenna
  ANT3 = Antenna
  UP = Antenna
  DWN = Antenna
  LFT = Antenna
  RGT = Antenna
  LED1 = Antenna
  MID = Antenna
  GND = Antenna
  NTE5 = Antenna
  NTE4 = Antenna
  NTE3 = Antenna
  NTE2 = Antenna
  NTE1 = Antenna
  LED2 = Antenna
  LED3 = Antenna
  LED4 = Antenna
  5V+ = Antenna
  220 = Resistor [tolerance=±5% power=0.25 resistance=220 package=THT]
  220_2 = Resistor [tolerance=±5% power=0.25 resistance=220 package=THT]
  220_3 = Resistor [tolerance=±5% power=0.25 resistance=220 package=THT]
  220_4 = Resistor [tolerance=±5% power=0.25 resistance=220 package=THT]
  STRT = Antenna
  SLCT = Antenna
  GND_2 = Antenna
  TUP = Antenna
  TDWM = Antenna
  GND_3 = Antenna
  5V = Antenna
  TRML = Antenna
  GND_4 = Antenna
  SLD = Antenna
  3_3V = Antenna
  GND_5 = Antenna
  220_5 = Resistor [tolerance=±5% power=0.25 resistance=220 package=THT]
  220_6 = Resistor [tolerance=±5% power=0.25 resistance=220 package=THT]
  ANT16 = Antenna
  ANT17 = Antenna
  ANT18 = Antenna
  ANT19 = Antenna
  ANT22 = Antenna
  - = Antenna
  + = Antenna

nets:
  N1: Part1.D1/TX, 220_6.Pin_1
  N2: Part1.D2, UP.antenna_lead
  N3: Part1.D3, DWN.antenna_lead
  N4: Part1.D4, LFT.antenna_lead
  N5: Part1.D5, RGT.antenna_lead
  N6: Part1.D6, 220.Pin_0
  N7: Part1.D7, MID.antenna_lead
  N8: Part1.D8, 220_2.Pin_0
  N9: Part1.D9, 220_3.Pin_0
  N10: Part1.D10, 220_4.Pin_0
  N11: Part1.D11/MOSI, TUP.antenna_lead
  N12: Part1.D12/MISO, TDWM.antenna_lead
  N13: Part1.VIN, ANT22.antenna_lead
  N14: Part1.GND, ANT3.antenna_lead, GND_4.antenna_lead, ANT16.antenna_lead
  N15: Part1.5V, 5V+.antenna_lead, 5V.antenna_lead, 220_5.Pin_1
  N16: Part1.A7, TRML.antenna_lead
  N17: Part1.A6, SLD.antenna_lead
  N18: Part1.A5, NTE5.antenna_lead
  N19: Part1.A4, NTE4.antenna_lead
  N20: Part1.A3, NTE3.antenna_lead
  N21: Part1.A2, NTE2.antenna_lead
  N22: Part1.A1, NTE1.antenna_lead
  N23: Part1.A0, STRT.antenna_lead
  N24: Part1.3V3, 3_3V.antenna_lead
  N25: Part1.D13/SCK, SLCT.antenna_lead
  N26: ANT1.antenna_lead, 220_6.Pin_0
  N27: ANT2.antenna_lead, 220_5.Pin_0
  N28: LED1.antenna_lead, 220.Pin_1
  N29: GND.antenna_lead, GND_2.antenna_lead, GND_3.antenna_lead, GND_5.antenna_lead
  N30: LED2.antenna_lead, 220_2.Pin_1
  N31: LED3.antenna_lead, 220_3.Pin_1
  N32: LED4.antenna_lead, 220_4.Pin_1
  N33: ANT17.antenna_lead, -.antenna_lead
  N34: ANT18.antenna_lead, ANT19.antenna_lead, +.antenna_lead

notes:
  www.CalmyJane.com
  MidiHero
  BE NICE!
  9V
