# Fritzing sketch SmallSchematic (saved by Fritzing 0.9.10b)
circuit board: 5.81051cm x 4.81608cm
breadboards: 1

parts:
  Part1 = Arduino Nano (Rev3.0)
  R1 = Resistor [tolerance=±5% power=0.25 resistance=220 package=THT]
  C1 = Ceramic Capacitor [capacitance=100nF voltage=35V package="100 mil [THT, multilayer]"]
  C2 = Ceramic Capacitor [capacitance=100nF voltage=35V package="100 mil [THT, multilayer]"]
  C3 = Ceramic Capacitor [capacitance=100nF voltage=35V package="100 mil [THT, multilayer]"]
  R4 = Resistor [tolerance=±5% power=0.25 resistance=220 package=THT]
  R5 = Resistor [tolerance=±5% power=0.25 resistance=220 package=THT]
  R6 = Resistor [tolerance=±5% power=0.25 resistance=220 package=THT]
  C4 = Ceramic Capacitor [capacitance=100nF voltage=35V package="100 mil [THT, multilayer]"]
  C5 = Ceramic Capacitor [capacitance=100nF voltage=35V package="100 mil [THT, multilayer]"]
  C6 = Ceramic Capacitor [capacitance=100nF voltage=35V package="100 mil [THT, multilayer]"]
  R7 = Resistor [tolerance=±5% power=0.25 resistance=220 package=THT]
  R8 = Resistor [tolerance=±5% power=0.25 resistance=220 package=THT]
  R9 = Resistor [tolerance=±5% power=0.25 resistance=220 package=THT]
  C7 = Ceramic Capacitor [capacitance=100nF voltage=35V package="100 mil [THT, multilayer]"]
  C8 = Ceramic Capacitor [capacitance=100nF voltage=35V package="100 mil [THT, multilayer]"]
  C9 = Ceramic Capacitor [capacitance=100nF voltage=35V package="100 mil [THT, multilayer]"]
  R11 = Resistor [tolerance=±5% power=0.25 resistance=220 package=THT]
  C10 = Ceramic Capacitor [capacitance=100nF voltage=35V package="100 mil [THT, multilayer]"]
  C11 = Ceramic Capacitor [capacitance=100nF voltage=35V package="100 mil [THT, multilayer]"]
  C12 = Ceramic Capacitor [capacitance=100nF voltage=35V package="100 mil [THT, multilayer]"]
  C13 = Ceramic Capacitor [capacitance=100nF voltage=35V package="100 mil [THT, multilayer]"]
  C14 = Ceramic Capacitor [capacitance=100nF voltage=35V package="100 mil [THT, multilayer]"]
  C15 = Ceramic Capacitor [capacitance=100nF voltage=35V package="100 mil [THT, multilayer]"]
  C16 = Ceramic Capacitor [capacitance=100nF voltage=35V package="100 mil [THT, multilayer]"]
  C17 = Ceramic Capacitor [capacitance=100nF voltage=35V package="100 mil [THT, multilayer]"]
  C18 = Ceramic Capacitor [capacitance=100nF voltage=35V package="100 mil [THT, multilayer]"]
  C19 = Ceramic Capacitor [capacitance=100nF voltage=35V package="100 mil [THT, multilayer]"]
  C20 = Ceramic Capacitor [capacitance=100nF voltage=35V package="100 mil [THT, multilayer]"]
  C21 = Ceramic Capacitor [capacitance=100nF voltage=35V package="100 mil [THT, multilayer]"]
  C22 = Ceramic Capacitor [capacitance=100nF voltage=35V package="100 mil [THT, multilayer]"]
  C23 = Ceramic Capacitor [capacitance=100nF voltage=35V package="100 mil [THT, multilayer]"]
  C24 = Ceramic Capacitor [capacitance=100nF voltage=35V package="100 mil [THT, multilayer]"]
  C25 = Ceramic Capacitor [capacitance=100nF voltage=35V package="100 mil [THT, multilayer]"]
  C26 = Ceramic Capacitor [capacitance=100nF voltage=35V package="100 mil [THT, multilayer]"]
  C27 = Ceramic Capacitor [capacitance=100nF voltage=35V package="100 mil [THT, multilayer]"]
  C28 = Ceramic Capacitor [capacitance=100nF voltage=35V package="100 mil [THT, multilayer]"]
  C29 = Ceramic Capacitor [capacitance=100nF voltage=35V package="100 mil [THT, multilayer]"]
  C30 = Ceramic Capacitor [capacitance=100nF voltage=35V package="100 mil [THT, multilayer]"]
  R12 = Resistor [tolerance=±5% power=0.25 resistance=220 package=THT]
  R13 = Resistor [tolerance=±5% power=0.25 resistance=220 package=THT]
  R14 = Resistor [tolerance=±5% power=0.25 resistance=220 package=THT]
  R15 = Resistor [tolerance=±5% power=0.25 resistance=220 package=THT]
  R16 = Resistor [tolerance=±5% power=0.25 resistance=220 package=THT]
  R17 = Resistor [tolerance=±5% power=0.25 resistance=220 package=THT]
  R18 = Resistor [tolerance=±5% power=0.25 resistance=220 package=THT]
  R19 = Resistor [tolerance=±5% power=0.25 resistance=220 package=THT]
  R20 = Resistor [tolerance=±5% power=0.25 resistance=220 package=THT]
  R21 = Resistor [tolerance=±5% power=0.25 resistance=220 package=THT]
  R22 = Resistor [tolerance=±5% power=0.25 resistance=220 package=THT]
  R23 = Resistor [tolerance=±5% power=0.25 resistance=220 package=THT]
  S1 = Toggle Switch [package=THT]
  R24 = Resistor [tolerance=±5% power=0.25 resistance=220 package=THT]
  C31 = Ceramic Capacitor [capacitance=100nF voltage=35V package="100 mil [THT, multilayer]"]
  C39 = Ceramic Capacitor [capacitance=100nF voltage=35V package="100 mil [THT, multilayer]"]
  C40 = Ceramic Capacitor [capacitance=100nF voltage=35V package="100 mil [THT, multilayer]"]
  C41 = Ceramic Capacitor [capacitance=100nF voltage=35V package="100 mil [THT, multilayer]"]
  C42 = Ceramic Capacitor [capacitance=100nF voltage=35V package="100 mil [THT, multilayer]"]
  C43 = Ceramic Capacitor [capacitance=100nF voltage=35V package="100 mil [THT, multilayer]"]
  C44 = Ceramic Capacitor [capacitance=100nF voltage=35V package="100 mil [THT, multilayer]"]
  ANT15 = Antenna
  ANT16 = Antenna
  ANT17 = Antenna
  ANT18 = Antenna
  ANT19 = Antenna
  ANT20 = Antenna
  ANT21 = Antenna
  ANT22 = Antenna
  ANT23 = Antenna
  ANT24 = Antenna
  ANT25 = Antenna
  ANT26 = Antenna
  ANT27 = Antenna
  ANT28 = Antenna
  ANT29 = Antenna
  ANT30 = Antenna
  ANT31 = Antenna
  S2 = Toggle Switch [package=THT]
  R25 = Resistor [tolerance=±5% power=0.25 resistance=220 package=THT]

nets:
  N1: Part1.D1/TX, C16.0, C16.1, R23.Pin_1
  N2: Part1.D0/RX, C23.0, C23.1
  N3: Part1.RESET, C13.0, C13.1, C29.0, C29.1
  N4: Part1.GND, C15.0, C15.1, C28.0, C28.1, R12.Pin_0, R13.Pin_0, R14.Pin_0, R15.Pin_0, R16.Pin_0, R18.Pin_0, R19.Pin_0, S1.L1, C31.0, C31.1, ANT16.antenna_lead, ANT21.antenna_lead, ANT29.antenna_lead, R25.Pin_1
  N5: Part1.D2, C22.0, C22.1, R13.Pin_1
  N6: Part1.D3, C20.0, C20.1, R14.Pin_1
  N7: Part1.D4, C19.0, C19.1, R15.Pin_1
  N8: Part1.D5, C21.0, C21.1, R16.Pin_1
  N9: Part1.D6, C25.0, C25.1, R17.Pin_1
  N10: Part1.D7, C18.0, C18.1, R18.Pin_1
  N11: Part1.D8, C24.0, C24.1, R19.Pin_1
  N12: Part1.D9, C26.0, C26.1, R20.Pin_1
  N13: Part1.D10, C17.0, C17.1, R22.Pin_1
  N14: Part1.D11/MOSI, C27.0, C27.1, R21.Pin_1
  N15: Part1.D12/MISO, C30.0, C30.1, R12.Pin_1
  N16: Part1.VIN, C14.0, C14.1, ANT15.antenna_lead, ANT22.antenna_lead
  N17: Part1.5V, C11.0, C11.1, S1.L2, R24.Pin_1, C39.0, C39.1, C40.0, C40.1, C41.0, C41.1, C42.0, C42.1, C43.0, C43.1, C44.0, C44.1
  N18: Part1.A7, C12.0, C12.1, S1.COM, R25.Pin_0
  N19: Part1.A6, R11.Pin_0, C10.0, C10.1
  N20: Part1.A5, R9.Pin_0, C8.0, C8.1
  N21: Part1.A4, R7.Pin_0, C9.0, C9.1
  N22: Part1.A3, R8.Pin_0, C7.0, C7.1
  N23: Part1.A2, R6.Pin_0, C5.0, C5.1
  N24: Part1.A1, R4.Pin_0, C6.0, C6.1
  N25: Part1.A0, R5.Pin_0, C4.0, C4.1, S2.COM
  N26: Part1.AREF, C3.0, C3.1
  N27: Part1.3V3, C2.0, C2.1, S2.L2
  N28: Part1.D13/SCK, R1.Pin_0, C1.0, C1.1
  N29: R1.Pin_1, R4.Pin_1, R5.Pin_1, R6.Pin_1, R7.Pin_1, R8.Pin_1, R9.Pin_1, R11.Pin_1, S2.L1
  N30: R17.Pin_0, ANT26.antenna_lead
  N31: R20.Pin_0, ANT25.antenna_lead
  N32: R21.Pin_0, ANT23.antenna_lead
  N33: R22.Pin_0, ANT24.antenna_lead
  N34: R23.Pin_0, ANT28.antenna_lead
  N35: R24.Pin_0, ANT27.antenna_lead
  N36: ANT17.antenna_lead, ANT20.antenna_lead, ANT31.antenna_lead
  N37: ANT18.antenna_lead, ANT19.antenna_lead, ANT30.antenna_lead

notes:
  10k
  220
  www.CalmyJane.com
  BE NICE!
  MidiHero Guitar Controller Board
  +
  -
  D2
  D3
  D4
  D5
  D6
  D7
  D8
  D9
  D10
  D11
  D12
  D13
  A0
  A1
  A2
  A3
  Aref
  A4
  3,3V
  A5
  A6
  5V
  A7
  RST
  GND
  Vin
  Rx
  Tx
