# Fritzing sketch Schematic (saved by Fritzing 0.9.10b)

parts:
  Arduino_Nano = Arduino Nano (Rev3.0)
  Tremolo = Trimmer Potentiometer [maximum_resistance=25kΩ knob_status=50% power=0.5W package=THT]
  R8 = Resistor [tolerance=±5% power=0.25 resistance=10k package=THT]
  R10 = Resistor [tolerance=±5% power=0.25 resistance=10k package=THT]
  R11 = Resistor [tolerance=±5% power=0.25 resistance=10k package=THT]
  R12 = Resistor [tolerance=±5% power=0.25 resistance=10k package=THT]
  R13 = Resistor [tolerance=±5% power=0.25 resistance=10k package=THT]
  R14 = Resistor [tolerance=±5% power=0.25 resistance=10k package=THT]
  R1 = Resistor [tolerance=±5% power=0.25 resistance=10k package=THT]
  MidiOutput = DIN-5 jack (MIDI) [package=THT]
  R2 = Resistor [tolerance=±5% power=0.25 resistance=220 package=THT]
  R2_2 = Resistor [tolerance=±5% power=0.25 resistance=220 package=THT]
  Neck_Connector = longpad pin header, 7 pins [form="long pad"]
  HeroPower_Board = longpad pin header, 8 pins [form="long pad"]
  R3 = Resistor [tolerance=±5% power=0.25 resistance=220 package=THT]
  R17 = Resistor [tolerance=±5% power=0.25 resistance=220 package=THT]
  R18 = Resistor [tolerance=±5% power=0.25 resistance=220 package=THT]
  R19 = Resistor [tolerance=±5% power=0.25 resistance=220 package=THT]
  R20 = Resistor [tolerance=±5% power=0.25 resistance=10k package=THT]
  R21 = Resistor [tolerance=±5% power=0.25 resistance=10k package=THT]
  R22 = Resistor [tolerance=±5% power=0.25 resistance=10k package=THT]
  R23 = Resistor [tolerance=±5% power=0.25 resistance=10k package=THT]
  R24 = Resistor [tolerance=±5% power=0.25 resistance=10k package=THT]
  R25 = Resistor [tolerance=±5% power=0.25 resistance=10k package=THT]
  R26 = Resistor [tolerance=±5% power=0.25 resistance=10k package=THT]
  R4 = Resistor [tolerance=±5% power=0.25 resistance=10k package=THT]
  D-pad_Board = longpad pin header, 8 pins [form="long pad"]
  Trigger_Board = longpad pin header, 3 pins [form="long pad"]
  Midi_Connector = longpad pin header, 3 pins [form="long pad"]
  Midi_Connector_Plug = longpad pin header, 3 pins [form="long pad"]
  Tremolo_2 = longpad pin header, 3 pins [form="long pad"]
  Tremolo_3 = longpad pin header, 3 pins [form="long pad"]
  D-pad_Board_2 = longpad pin header, 8 pins [form="long pad"]
  Shift = Pushbutton [package=THT]
  Up = Pushbutton [package=THT]
  Down = Pushbutton [package=THT]
  Left = Pushbutton [package=THT]
  Right = Pushbutton [package=THT]
  D-pad_Middle = Pushbutton [package=THT]
  Note6 = Pushbutton [package=THT]
  Note5 = Pushbutton [package=THT]
  Note4 = Pushbutton [package=THT]
  Note1 = Pushbutton [package=THT]
  Note2 = Pushbutton [package=THT]
  Note3 = Pushbutton [package=THT]
  Neck_Connector_2 = longpad pin header, 7 pins [form="long pad"]
  Trigger_Up = Pushbutton [package=THT]
  Trigger_Down = Pushbutton [package=THT]
  Trigger_Board_2 = longpad pin header, 3 pins [form="long pad"]
  HeroPower_(Start) = Pushbutton [package=THT]
  Select = Pushbutton [package=THT]
  LED1 = LED - 5mm [color="Red (633nm)" current=0.030 package="5 mm [THT]"]
  LED2 = LED - 5mm [color="Red (633nm)" current=0.030 package="5 mm [THT]"]
  LED3 = LED - 5mm [color="Red (633nm)" current=0.030 package="5 mm [THT]"]
  LED4 = LED - 5mm [color="Red (633nm)" current=0.030 package="5 mm [THT]"]
  HeroPower_Board_2 = longpad pin header, 8 pins [form="long pad"]

nets:
  N1: Arduino_Nano.D1/TX, R2_2.Pin_0
  N2: Arduino_Nano.GND, R8.Pin_0, R10.Pin_0, R11.Pin_0, R12.Pin_0, R13.Pin_0, R14.Pin_0, R1.Pin_0, R20.Pin_1, R21.Pin_1, R22.Pin_1, R23.Pin_1, R24.Pin_1, R25.Pin_1, R26.Pin_1, R4.Pin_1, Midi_Connector.pin2, Tremolo_2.pin1
  N3: Arduino_Nano.D2, R19.Pin_0
  N4: Arduino_Nano.D3, R18.Pin_0
  N5: Arduino_Nano.D4, R17.Pin_0
  N6: Arduino_Nano.D5, R3.Pin_0
  N7: Arduino_Nano.D6, HeroPower_Board.pin4, R20.Pin_0
  N8: Arduino_Nano.D7, Neck_Connector.pin7, R21.Pin_0
  N9: Arduino_Nano.D8, Neck_Connector.pin6, R22.Pin_0
  N10: Arduino_Nano.D9, Neck_Connector.pin5, R23.Pin_0
  N11: Arduino_Nano.D10, Neck_Connector.pin4, R24.Pin_0
  N12: Arduino_Nano.D11/MOSI, Neck_Connector.pin3, R25.Pin_0
  N13: Arduino_Nano.D12/MISO, Neck_Connector.pin2, R26.Pin_0
  N14: Arduino_Nano.5V, R2.Pin_0, Neck_Connector.pin1, HeroPower_Board.pin1, HeroPower_Board.pin2, D-pad_Board.pin7, D-pad_Board.pin8, Trigger_Board.pin2, Tremolo_2.pin3
  N15: Arduino_Nano.A7, R8.Pin_1, D-pad_Board.pin1
  N16: Arduino_Nano.A6, R10.Pin_1, D-pad_Board.pin2
  N17: Arduino_Nano.A5, R11.Pin_1, D-pad_Board.pin3
  N18: Arduino_Nano.A4, R12.Pin_1, D-pad_Board.pin4
  N19: Arduino_Nano.A3, R13.Pin_1, D-pad_Board.pin5
  N20: Arduino_Nano.A2, R14.Pin_1, D-pad_Board.pin6
  N21: Arduino_Nano.A1, R1.Pin_1, Trigger_Board.pin1
  N22: Arduino_Nano.A0, Tremolo_2.pin2
  N23: Arduino_Nano.D13/SCK, R4.Pin_0, Trigger_Board.pin3
  N24: Tremolo.leg1, Tremolo_3.pin1
  N25: Tremolo.wiper, Tremolo_3.pin2
  N26: Tremolo.leg2, Tremolo_3.pin3
  N27: MidiOutput.5, Midi_Connector_Plug.pin1
  N28: MidiOutput.2, Midi_Connector_Plug.pin2
  N29: MidiOutput.4, Midi_Connector_Plug.pin3
  N30: R2.Pin_1, Midi_Connector.pin1
  N31: R2_2.Pin_1, Midi_Connector.pin3
  N32: HeroPower_Board.pin5, R3.Pin_1
  N33: HeroPower_Board.pin6, R17.Pin_1
  N34: HeroPower_Board.pin7, R18.Pin_1
  N35: HeroPower_Board.pin8, R19.Pin_1
  N36: D-pad_Board_2.pin1, D-pad_Middle.leg0
  N37: D-pad_Board_2.pin2, Right.leg0
  N38: D-pad_Board_2.pin3, Left.leg0
  N39: D-pad_Board_2.pin4, Down.leg0
  N40: D-pad_Board_2.pin5, Up.leg0
  N41: D-pad_Board_2.pin6, Shift.leg0
  N42: D-pad_Board_2.pin7, Shift.leg1
  N43: D-pad_Board_2.pin8, Up.leg1, Down.leg1, Left.leg1, Right.leg1, D-pad_Middle.leg1
  N44: Note6.leg0, Neck_Connector_2.pin7
  N45: Note6.leg1, Note5.leg1, Note4.leg1, Note1.leg1, Note2.leg1, Note3.leg1, Neck_Connector_2.pin1
  N46: Note5.leg0, Neck_Connector_2.pin6
  N47: Note4.leg0, Neck_Connector_2.pin5
  N48: Note1.leg0, Neck_Connector_2.pin2
  N49: Note2.leg0, Neck_Connector_2.pin3
  N50: Note3.leg0, Neck_Connector_2.pin4
  N51: Trigger_Up.leg0, Trigger_Board_2.pin1
  N52: Trigger_Up.leg1, Trigger_Down.leg1, Trigger_Board_2.pin2
  N53: Trigger_Down.leg0, Trigger_Board_2.pin3
  N54: HeroPower_(Start).leg0, HeroPower_Board_2.pin4
  N55: HeroPower_(Start).leg1, Select.leg1, HeroPower_Board_2.pin2
  N56: Select.leg0, HeroPower_Board_2.pin3
  N57: LED1.cathode, HeroPower_Board_2.pin5
  N58: LED1.anode, LED2.anode, LED3.anode, LED4.anode, HeroPower_Board_2.pin1
  N59: LED2.cathode, HeroPower_Board_2.pin6
  N60: LED3.cathode, HeroPower_Board_2.pin7
  N61: LED4.cathode, HeroPower_Board_2.pin8
