# Fritzing sketch pcb (saved by Fritzing 0.9.10b)
circuit board: 9.50694cm x 7.40505cm
breadboards: 1

parts:
  Part1 = Arduino Nano (Rev3.0)
  R1 = Resistor [tolerance=±5% power=0.25 resistance=220 package=THT]
  part = shrouded pin header, 8 pins [form="♂ (shrouded male)"]
  J4 = shrouded pin header, 8 pins [form="♂ (shrouded male)"]
  R2 = Resistor [tolerance=±5% power=0.25 resistance=220 package=THT]
  R3 = Resistor [tolerance=±5% power=0.25 resistance=220 package=THT]
  R4 = Resistor [tolerance=±5% power=0.25 resistance=220 package=THT]
  R5 = Resistor [tolerance=±5% power=0.25 resistance=10k package=THT]
  R6 = Resistor [tolerance=±5% power=0.25 resistance=10k package=THT]
  R7 = Resistor [tolerance=±5% power=0.25 resistance=10k package=THT]
  R8 = Resistor [tolerance=±5% power=0.25 resistance=10k package=THT]
  R9 = Resistor [tolerance=±5% power=0.25 resistance=10k package=THT]
  R10 = Resistor [tolerance=±5% power=0.25 resistance=10k package=THT]
  R11 = Resistor [tolerance=±5% power=0.25 resistance=10k package=THT]
  J5 = shrouded pin header, 8 pins [form="♂ (shrouded male)"]
  R12 = Resistor [tolerance=±5% power=0.25 resistance=10k package=THT]
  R13 = Resistor [tolerance=±5% power=0.25 resistance=10k package=THT]
  R14 = Resistor [tolerance=±5% power=0.25 resistance=10k package=THT]
  R15 = Resistor [tolerance=±5% power=0.25 resistance=10k package=THT]
  R17 = Resistor [tolerance=±5% power=0.25 resistance=10k package=THT]
  R18 = Resistor [tolerance=±5% power=0.25 resistance=10k package=THT]
  R19 = Resistor [tolerance=±5% power=0.25 resistance=10k package=THT]
  R20 = Resistor [tolerance=±5% power=0.25 resistance=10k package=THT]
  J6 = shrouded pin header, 8 pins [form="♂ (shrouded male)"]
  part_2 = shrouded pin header, 8 pins [form="♂ (shrouded male)"]
  R22 = Resistor [tolerance=±5% power=0.25 resistance=220 package=THT]
  R21 = Resistor [tolerance=±5% power=0.25 resistance=220 package=THT]

nets:
  N1: Part1.D1/TX, R14.Pin_1
  N2: Part1.GND, J4.pin7, R10.Pin_0, J6.pin7
  N3: Part1.D2, R13.Pin_1
  N4: Part1.D3, R18.Pin_1
  N5: Part1.D4, R15.Pin_1
  N6: Part1.D5, R17.Pin_1
  N7: Part1.D6, R12.Pin_1
  N8: Part1.D7, R19.Pin_1
  N9: Part1.D8, R20.Pin_1
  N10: Part1.D9, J4.pin8, J5.pin7, J6.pin1, J6.pin2, part_2.pin2, part_2.pin3
  N11: Part1.D10, part_2.pin7
  N12: Part1.D11/MOSI, R12.Pin_0, R13.Pin_0, R14.Pin_0, R15.Pin_0, R17.Pin_0, R18.Pin_0, R19.Pin_0, R20.Pin_0, J6.pin3, part_2.pin1, part_2.pin8, R22.Pin_1
  N13: Part1.D12/MISO, part_2.pin5
  N14: Part1.VIN, R11.Pin_0
  N15: Part1.RESET, R9.Pin_0
  N16: Part1.5V, R8.Pin_0
  N17: Part1.A7, R7.Pin_0
  N18: Part1.A6, R6.Pin_0
  N19: Part1.A5, part.pin7, R5.Pin_0
  N20: Part1.A4, R4.Pin_0
  N21: Part1.A3, R3.Pin_0
  N22: Part1.A2, R2.Pin_0
  N23: Part1.A1, R1.Pin_0
  N24: Part1.A0, R5.Pin_1, R6.Pin_1, R7.Pin_1, R8.Pin_1, R9.Pin_1, R10.Pin_1, R11.Pin_1
  N25: Part1.D13/SCK, R21.Pin_1
  N26: R1.Pin_1, part.pin4
  N27: part.pin1, R4.Pin_1
  N28: part.pin2, R3.Pin_1
  N29: part.pin3, R2.Pin_1
  N30: part.pin5, part.pin6
  N31: part_2.pin4, R21.Pin_0
  N32: part_2.pin6, R22.Pin_0

notes:
  +5V/+5V
  GND/RST
  GND/MIDI1
  MidiTX/Vin
  +5V/UP
  +5V/Trm
  GND/Dwn
  ---/---
  DUP/---
  DDwn/+5V
  DLft/DMid
  DRgt/Shft
  Nte4/+5V
  Nte3/Nte5
  Nte2/---
  Nte1/Nte6
  LED1/---
  LED2/Slct
  LED3/+5V
  LED4/+5V
  made by Calmy Jane
  www.CalmyJane.com
